// Logisim project control-logic.circ as structural Verilog: 1 circuit, main circuit control_logic
module control_logic (
  input  [31:0] inst,
  input  BrEq,
  input  BrLt,
  output PCSel,
  output RegWEn,
  output [2:0] ImmSel,
  output BrUn,
  output ASel,
  output BSel,
  output [3:0] ALUSel,
  output MemRW,
  output [1:0] WBSel,
  output CSRSel,
  output CSRWen
);

  wire auipc, comparator_12_eq, CSR_type, I_type, jal, jalr, L_type, lui, not_1_out, not_2_out, R_type,
       S_type, SB_type, Zero;
  wire [0:0] SB_logic;
  wire [3:0] priority_encoder_1_p9;
  wire [11:10] R_logic;
  wire [11:11] I_logic;
  wire [15:0] rom_1_data;

  Comparator #(.mode("unsigned"), .width(7)) comparator_1 (.a(inst[6:0]), .b(7'b0010011), .eq(I_type));  // open: gt, lt
  Comparator #(.mode("unsigned"), .width(7)) comparator_2 (.a(inst[6:0]), .b(7'b0110011), .eq(R_type));  // open: gt, lt
  Comparator #(.mode("unsigned"), .width(7)) comparator_3 (
    .a(inst[6:0]), .b(7'b1100011), .eq(SB_type));  // open: gt, lt
  Comparator #(.mode("unsigned"), .width(7)) comparator_4 (.a(inst[6:0]), .b(7'b0000011), .eq(L_type));  // open: gt, lt
  Comparator #(.mode("unsigned"), .width(7)) comparator_5 (.a(inst[6:0]), .b(7'b0100011), .eq(S_type));  // open: gt, lt
  Comparator #(.mode("unsigned"), .width(7)) comparator_6 (.a(inst[6:0]), .b(7'b0010111), .eq(auipc));  // open: gt, lt
  Comparator #(.mode("unsigned"), .width(7)) comparator_7 (.a(inst[6:0]), .b(7'b0110111), .eq(lui));  // open: gt, lt
  Comparator #(.mode("unsigned"), .width(7)) comparator_8 (.a(inst[6:0]), .b(7'b1101111), .eq(jal));  // open: gt, lt
  Comparator #(.mode("unsigned"), .width(7)) comparator_9 (.a(inst[6:0]), .b(7'b1100111), .eq(jalr));  // open: gt, lt
  Comparator #(.mode("unsigned"), .width(7)) comparator_10 (
    .a(inst[6:0]), .b(7'b1110011), .eq(CSR_type));  // open: gt, lt
  Comparator #(.mode("unsigned"), .width(32)) comparator_11 (.a(inst), .b({32{1'b0}}), .eq(Zero));  // open: gt, lt
  ROM #(.addrWidth(6), .dataWidth(16)) rom_1 (.data(rom_1_data));  // open: addr
  Comparator #(.mode("unsigned"), .width(3)) comparator_12 (
    .a(inst[14:12]), .b(3'b101), .eq(comparator_12_eq));  // open: gt, lt
  and and_1 (I_logic[11], comparator_12_eq, inst[30]);
  not not_1 (not_1_out, BrEq);
  not not_2 (not_2_out, BrLt);
  or or_1 (R_logic[10], inst[14], inst[30]);
  or or_2 (R_logic[11], inst[30], inst[25]);
  Multiplexer #(.enable("false"), .select(2)) multiplexer_1 (
    .in0(BrEq), .in1(not_1_out), .in2(BrLt), .in3(not_2_out), .out(SB_logic[0]), .sel({inst[14], inst[12]}));
  // Priority_Encoder #(.select(4)) priority_encoder_1: pin names not known; wires that end beside it: Zero, I_type, R_type, SB_type, L_type, S_type, auipc, lui, priority_encoder_1_p9, jal, jalr, CSR_type
  Multiplexer #(.enable("false"), .select(4), .width(17)) multiplexer_2 (
    .in0({17{1'b0}}), .in1({{5{1'b0}}, I_logic[11], inst[14:12], 8'h82}),
    .in2({{5{1'b0}}, R_logic, inst[13:12], 8'h2}), .in3({11'h3, inst[13], 4'b0010, SB_logic[0]}),
    .in4(17'h2082), .in5(17'h1088), .in6(17'hce), .in7(17'hf8e), .in8(17'h40d3), .in9(17'h4083),
    .in10({1'b1, inst[14], 15'h14}),
    .out({CSRWen, CSRSel, WBSel, MemRW, ALUSel, BSel, ASel, BrUn, ImmSel, RegWEn, PCSel}),
    .sel(priority_encoder_1_p9));  // open: in11, in12, in13, in14, in15

  // Other names for the same wires on the sheet: CSR_logic[15] = inst[14]; func3[2:0] = inst[14:12];
  //   I_logic[10:8] = inst[14:12]; opcode[6:0] = inst[6:0]; func7[6:0] = inst[31:25]; R_logic[9:8] = inst[13:12];
  //   SB_logic[5] = inst[13]

  // Notes on the sheet:
  //   INPUTS to your circuit
  //   Connect ROM Input here ->
  //   contents of rom_1 (hex, n*v repeats v):
  //   15*0 8200 8220 8240 8280 82a0 83a0 82c0 82e0
  //   ROM FOR CONTROL LOGIC
  //   DON'T CHANGE THE LOCATIONS OF THE INPUTS AND OUTPUTS!
  //   OUTPUT from your circuit
  //   CLOSE
  //   WIRE
  //   TO
  //   USE
  //   ROM
  //   Reminder: Use combinational logic for PCSel
endmodule
