// Logisim project cpu.circ as structural Verilog: 2 circuits, main circuit cpu
module cpu (
  input  clk,
  input  [31:0] INSTRUCTION,
  input  [31:0] MEM_READ_DATA,
  output [31:0] MEM_WRITE_ADDRESS,
  output [31:0] PROGRAM_COUNTER,
  output [31:0] ra,
  output [31:0] sp,
  output [31:0] t0,
  output [31:0] t1,
  output [31:0] t2,
  output [31:0] s0,
  output [31:0] s1,
  output [31:0] a0,
  output [31:0] tohost,
  output [3:0] MEM_WRITE_ENABLE,
  output [31:0] MEM_WRITE_DATA
);

  wire branch_comp_1_breq, branch_comp_1_brlt, control_logic_1_asel, control_logic_1_brun,
       control_logic_1_bsel, control_logic_1_csrsel, control_logic_1_csrwen, control_logic_1_memrw,
       control_logic_1_regwen, PCSel;
  wire [1:0] control_logic_1_wbsel;
  wire [2:0] control_logic_1_immsel;
  wire [3:0] control_logic_1_alusel;
  wire [31:0] adder_1_out, adder_2_out, Curr_Inst, Curr_PC, imm, mem_control_1_outputdata, multiplexer_1_out,
       multiplexer_2_out, multiplexer_3_out, multiplexer_4_out, multiplexer_6_out, Result, rs1, rs2,
       Write_Back;

  Adder #(.width(32)) adder_1 (.a(PROGRAM_COUNTER), .b(32'h4), .out(adder_1_out));  // open: cin, cout
  Register #(.width(32)) Inst_Reg (.D(multiplexer_1_out), .clk(clk), .Q(Curr_Inst));  // open: en, clr
  Multiplexer #(.enable("false"), .width(32)) multiplexer_1 (
    .in0(INSTRUCTION), .in1(32'h13), .out(multiplexer_1_out), .sel(PCSel));
  Register #(.width(32)) PC (.D(multiplexer_2_out), .clk(clk), .Q(PROGRAM_COUNTER));  // open: en, clr
  Multiplexer #(.enable("false"), .width(32)) multiplexer_2 (
    .in0(adder_1_out), .in1(Result), .out(multiplexer_2_out), .sel(PCSel));
  Register #(.width(32)) register_1 (.D(PROGRAM_COUNTER), .clk(clk), .Q(Curr_PC));  // open: en, clr
  control_logic control_logic_1 (
    .CSRWen(control_logic_1_csrwen), .PCSel(PCSel), .RegWEn(control_logic_1_regwen),
    .ImmSel(control_logic_1_immsel), .BrUn(control_logic_1_brun), .ASel(control_logic_1_asel),
    .BSel(control_logic_1_bsel), .ALUSel(control_logic_1_alusel), .MemRW(control_logic_1_memrw),
    .WBSel(control_logic_1_wbsel), .CSRSel(control_logic_1_csrsel), .inst(Curr_Inst),
    .BrEq(branch_comp_1_breq), .BrLt(branch_comp_1_brlt));
  regfile regfile_1 (
    .rs1(Curr_Inst[19:15]), .rs2(Curr_Inst[24:20]), .rd(Curr_Inst[11:7]), .Write_Data(Write_Back),
    .RegWEn(control_logic_1_regwen), .clk(clk), .ra(ra), .sp(sp), .t0(t0), .t1(t1), .t2(t2), .s0(s0),
    .s1(s1), .a0(a0), .Read_Data_1(rs1), .Read_Data_2(rs2));
  imm_gen imm_gen_1 (.inst(Curr_Inst), .ImmSel(control_logic_1_immsel), .imm(imm));
  branch_comp branch_comp_1 (
    .BrEq(branch_comp_1_breq), .BrLt(branch_comp_1_brlt), .rs1(rs1), .rs2(rs2), .BrUn(control_logic_1_brun));
  Multiplexer #(.enable("false"), .width(32)) multiplexer_3 (
    .in0(rs1), .in1(Curr_PC), .out(multiplexer_3_out), .sel(control_logic_1_asel));
  Multiplexer #(.enable("false"), .width(32)) multiplexer_4 (
    .in0(rs2), .in1(imm), .out(multiplexer_4_out), .sel(control_logic_1_bsel));
  alu alu_1 (.Result(Result), .A(multiplexer_3_out), .B(multiplexer_4_out), .ALUSel(control_logic_1_alusel));
  mem_control mem_control_1 (
    .OutputData(mem_control_1_outputdata), .inst(Curr_Inst), .Address(Result), .rs2(rs2),
    .MemRW(control_logic_1_memrw), .clk(clk));
  Adder #(.width(32)) adder_2 (.a(Curr_PC), .b(32'h4), .out(adder_2_out));  // open: cin, cout
  Multiplexer #(.enable("false"), .select(2), .width(32)) multiplexer_5 (
    .in0(Result), .in1(mem_control_1_outputdata), .in2(adder_2_out), .out(Write_Back),
    .sel(control_logic_1_wbsel));  // open: in3
  Multiplexer #(.enable("false"), .width(32)) multiplexer_6 (
    .in0(rs1), .in1(imm), .out(multiplexer_6_out), .sel(control_logic_1_csrsel));
  // csr csr_1: pin names not known; wires that end beside it: Curr_Inst[31:20], multiplexer_6_out, control_logic_1_csrwen, clk, tohost

  // Notes on the sheet:
  //   Output to IMEM
  //   IMEM (do **NOT** move this)
  //   Inputs from IMEM
  //   It is OK to move the PC, RegFile, ALU, MEM, Branch Comp, Imm Gen, and Control Logic to wherever is most convenient for you when constructing your CPU, and to delete this text
  //   Inputs/Outputs for testing. Do **NOT** move these.
  //   Outputs To DMEM
  //   DMEM (do **NOT** move this)
  //   Inputs From DMEM
endmodule

module mem_control (
  input  MemRW,
  input  [31:0] inst,
  input  [31:0] Address,
  input  [31:0] rs2,
  input  clk,
  output [31:0] OutputData
);

  wire [3:0] decoder_1_out0, multiplexer_3_out, Write_En;
  wire [7:0] multiplexer_1_out;
  wire [15:0] multiplexer_2_out;
  wire [31:0] bit_extender_1_out, bit_extender_2_out, InputData, Write_Data;

  Multiplexer #(.enable("false"), .select(2), .width(8)) multiplexer_1 (
    .in0(InputData[7:0]), .in1(InputData[15:8]), .in2(InputData[23:16]), .in3(InputData[31:24]),
    .out(multiplexer_1_out), .sel(Address[1:0]));
  Multiplexer #(.enable("false"), .width(16)) multiplexer_2 (
    .in0(InputData[15:0]), .in1(InputData[31:16]), .out(multiplexer_2_out), .sel(Address[1]));
  Decoder #(.enable("false"), .select(2)) decoder_1 (
    .out0(decoder_1_out0[0]), .out1(decoder_1_out0[1]), .out2(decoder_1_out0[2]), .out3(decoder_1_out0[3]),
    .sel(Address[1:0]));
  Multiplexer #(.enable("false"), .width(4)) multiplexer_3 (
    .in0(4'b0011), .in1(4'b1100), .out(multiplexer_3_out), .sel(Address[1]));
  assign bit_extender_1_out = {{24{multiplexer_1_out[7]}}, multiplexer_1_out};  // Bit_Extender bit_extender_1
  assign bit_extender_2_out = {{16{multiplexer_2_out[15]}}, multiplexer_2_out};  // Bit_Extender bit_extender_2
  Multiplexer #(.select(2), .width(4)) multiplexer_4 (
    .in0(decoder_1_out0), .in1(multiplexer_3_out), .in2(4'b1111), .out(Write_En), .sel(inst[13:12]),
    .en(MemRW));  // open: in3
  Multiplexer #(.enable("false"), .select(2), .width(32)) multiplexer_5 (
    .in0({rs2[7:0], rs2[7:0], rs2[7:0], rs2[7:0]}), .in1({rs2[15:0], rs2[15:0]}), .in2(rs2),
    .out(Write_Data), .sel(inst[13:12]));  // open: in3
  Multiplexer #(.enable("false"), .select(2), .width(32)) multiplexer_6 (
    .in0(bit_extender_1_out), .in1(bit_extender_2_out), .in2(InputData), .out(OutputData), .sel(inst[13:12]));  // open: in3
  mem mem_1 (
    .Read_Data(InputData), .Address({Address[31:2], 2'b00}), .Write_En(Write_En), .Write_Data(Write_Data),
    .clk(clk));

  // Other names for the same wires on the sheet: low[1:0] = Address[1:0]; func3[2:0] = inst[14:12];
  //   OutputAddress[31:2] = Address[31:2]
endmodule
