// Logisim project mem.circ as structural Verilog: 1 circuit, main circuit mem
module mem (
  input  [31:0] Address,
  input  [3:0] Write_En,
  input  [31:0] Write_Data,
  input  clk,
  output [31:0] Read_Data
);

  RAM #(.addrWidth(14), .trigger("falling")) DMEM_0 (
    .addr(Address[15:2]), .we(Write_En[0]), .oe(1'b1), .clk(clk), .din(Write_Data[7:0]), .dout(Read_Data[7:0]));
  RAM #(.addrWidth(14), .trigger("falling")) DMEM_1 (
    .addr(Address[15:2]), .we(Write_En[1]), .oe(1'b1), .clk(clk), .din(Write_Data[15:8]),
    .dout(Read_Data[15:8]));
  RAM #(.addrWidth(14), .trigger("falling")) DMEM_2 (
    .addr(Address[15:2]), .we(Write_En[2]), .oe(1'b1), .clk(clk), .din(Write_Data[23:16]),
    .dout(Read_Data[23:16]));
  RAM #(.addrWidth(14), .trigger("falling")) DMEM_3 (
    .addr(Address[15:2]), .we(Write_En[3]), .oe(1'b1), .clk(clk), .din(Write_Data[31:24]),
    .dout(Read_Data[31:24]));
endmodule
