// Logisim project regfile.circ as structural Verilog: 1 circuit, main circuit regfile
module regfile (
  input  [4:0] rs1,
  input  [4:0] rs2,
  input  [4:0] rd,
  input  [31:0] Write_Data,
  input  RegWEn,
  input  clk,
  output [31:0] ra,
  output [31:0] sp,
  output [31:0] t0,
  output [31:0] t1,
  output [31:0] t2,
  output [31:0] s0,
  output [31:0] s1,
  output [31:0] a0,
  output [31:0] Read_Data_1,
  output [31:0] Read_Data_2
);

  wire x1_WE, x2_WE, x3_WE, x4_WE, x5_WE, x6_WE, x7_WE, x8_WE, x9_WE, x10_WE, x11_WE, x12_WE, x13_WE, x14_WE,
       x15_WE, x16_WE, x17_WE, x18_WE, x19_WE, x20_WE, x21_WE, x22_WE, x23_WE, x24_WE, x25_WE, x26_WE,
       x27_WE, x28_WE, x29_WE, x30_WE, x31_WE;
  wire [31:0] a1, a2, a3, a4, a5, a6, a7, gp, s2, s3, s4, s5, s6, s7, s8, s9, s10, s11, t3, t4, t5, t6, tp;

  Demultiplexer #(.enable("false"), .select(5)) demultiplexer_1 (
    .out1(x1_WE), .out2(x2_WE), .out3(x3_WE), .out4(x4_WE), .out5(x5_WE), .out6(x6_WE), .out7(x7_WE),
    .out8(x8_WE), .out9(x9_WE), .out10(x10_WE), .out11(x11_WE), .out12(x12_WE), .out13(x13_WE),
    .out14(x14_WE), .out15(x15_WE), .out16(x16_WE), .out17(x17_WE), .out18(x18_WE), .out19(x19_WE),
    .out20(x20_WE), .out21(x21_WE), .out22(x22_WE), .out23(x23_WE), .out24(x24_WE), .out25(x25_WE),
    .out26(x26_WE), .out27(x27_WE), .out28(x28_WE), .out29(x29_WE), .out30(x30_WE), .out31(x31_WE),
    .in(RegWEn), .sel(rd));  // open: out0
  Register #(.width(32)) register_1 (.D(Write_Data), .en(x1_WE), .clk(clk), .Q(ra));  // open: clr
  Register #(.width(32)) register_2 (.D(Write_Data), .en(x5_WE), .clk(clk), .Q(t0));  // open: clr
  Register #(.width(32)) register_3 (.D(Write_Data), .en(x9_WE), .clk(clk), .Q(s1));  // open: clr
  Register #(.width(32)) register_4 (.D(Write_Data), .en(x13_WE), .clk(clk), .Q(a3));  // open: clr
  Register #(.width(32)) register_5 (.D(Write_Data), .en(x17_WE), .clk(clk), .Q(a7));  // open: clr
  Register #(.width(32)) register_6 (.D(Write_Data), .en(x21_WE), .clk(clk), .Q(s5));  // open: clr
  Register #(.width(32)) register_7 (.D(Write_Data), .en(x25_WE), .clk(clk), .Q(s9));  // open: clr
  Register #(.width(32)) register_8 (.D(Write_Data), .en(x29_WE), .clk(clk), .Q(t4));  // open: clr
  Register #(.width(32)) register_9 (.D(Write_Data), .en(x2_WE), .clk(clk), .Q(sp));  // open: clr
  Register #(.width(32)) register_10 (.D(Write_Data), .en(x6_WE), .clk(clk), .Q(t1));  // open: clr
  Register #(.width(32)) register_11 (.D(Write_Data), .en(x10_WE), .clk(clk), .Q(a0));  // open: clr
  Register #(.width(32)) register_12 (.D(Write_Data), .en(x14_WE), .clk(clk), .Q(a4));  // open: clr
  Register #(.width(32)) register_13 (.D(Write_Data), .en(x18_WE), .clk(clk), .Q(s2));  // open: clr
  Register #(.width(32)) register_14 (.D(Write_Data), .en(x22_WE), .clk(clk), .Q(s6));  // open: clr
  Register #(.width(32)) register_15 (.D(Write_Data), .en(x26_WE), .clk(clk), .Q(s10));  // open: clr
  Register #(.width(32)) register_16 (.D(Write_Data), .en(x30_WE), .clk(clk), .Q(t5));  // open: clr
  Multiplexer #(.enable("false"), .select(5), .width(32)) multiplexer_1 (
    .in0({32{1'b0}}), .in1(ra), .in2(sp), .in3(gp), .in4(tp), .in5(t0), .in6(t1), .in7(t2), .in8(s0),
    .in9(s1), .in10(a0), .in11(a1), .in12(a2), .in13(a3), .in14(a4), .in15(a5), .in16(a6), .in17(a7),
    .in18(s2), .in19(s3), .in20(s4), .in21(s5), .in22(s6), .in23(s7), .in24(s8), .in25(s9), .in26(s10),
    .in27(s11), .in28(t3), .in29(t4), .in30(t5), .in31(t6), .out(Read_Data_1), .sel(rs1));
  Register #(.width(32)) register_17 (.D(Write_Data), .en(x3_WE), .clk(clk), .Q(gp));  // open: clr
  Register #(.width(32)) register_18 (.D(Write_Data), .en(x7_WE), .clk(clk), .Q(t2));  // open: clr
  Register #(.width(32)) register_19 (.D(Write_Data), .en(x11_WE), .clk(clk), .Q(a1));  // open: clr
  Register #(.width(32)) register_20 (.D(Write_Data), .en(x15_WE), .clk(clk), .Q(a5));  // open: clr
  Register #(.width(32)) register_21 (.D(Write_Data), .en(x19_WE), .clk(clk), .Q(s3));  // open: clr
  Register #(.width(32)) register_22 (.D(Write_Data), .en(x23_WE), .clk(clk), .Q(s7));  // open: clr
  Register #(.width(32)) register_23 (.D(Write_Data), .en(x27_WE), .clk(clk), .Q(s11));  // open: clr
  Register #(.width(32)) register_24 (.D(Write_Data), .en(x31_WE), .clk(clk), .Q(t6));  // open: clr
  Register #(.width(32)) register_25 (.D(Write_Data), .en(x4_WE), .clk(clk), .Q(tp));  // open: clr
  Register #(.width(32)) register_26 (.D(Write_Data), .en(x8_WE), .clk(clk), .Q(s0));  // open: clr
  Register #(.width(32)) register_27 (.D(Write_Data), .en(x12_WE), .clk(clk), .Q(a2));  // open: clr
  Register #(.width(32)) register_28 (.D(Write_Data), .en(x16_WE), .clk(clk), .Q(a6));  // open: clr
  Register #(.width(32)) register_29 (.D(Write_Data), .en(x20_WE), .clk(clk), .Q(s4));  // open: clr
  Register #(.width(32)) register_30 (.D(Write_Data), .en(x24_WE), .clk(clk), .Q(s8));  // open: clr
  Register #(.width(32)) register_31 (.D(Write_Data), .en(x28_WE), .clk(clk), .Q(t3));  // open: clr
  Multiplexer #(.enable("false"), .select(5), .width(32)) multiplexer_2 (
    .in0({32{1'b0}}), .in1(ra), .in2(sp), .in3(gp), .in4(tp), .in5(t0), .in6(t1), .in7(t2), .in8(s0),
    .in9(s1), .in10(a0), .in11(a1), .in12(a2), .in13(a3), .in14(a4), .in15(a5), .in16(a6), .in17(a7),
    .in18(s2), .in19(s3), .in20(s4), .in21(s5), .in22(s6), .in23(s7), .in24(s8), .in25(s9), .in26(s10),
    .in27(s11), .in28(t3), .in29(t4), .in30(t5), .in31(t6), .out(Read_Data_2), .sel(rs2));

  // Other names for the same wires on the sheet: read_data1[31:0] = Read_Data_1; read_data2[31:0] = Read_Data_2;
  //   read_reg1[4:0] = rs1; read_reg2[4:0] = rs2; write_en = RegWEn; write_reg[4:0] = rd

  // Notes on the sheet:
  //   INPUTS to your circuit
  //   DON'T CHANGE THE LOCATIONS OF THE INPUTS AND OUTPUTS!
  //   These are DEBUG/TEST outputs from your circuit.
  //   OUTPUTS from your circuit
endmodule
